// Logisim project 74LS173.circ as structural Verilog: 1 circuit, main circuit IC74LS173
module IC74LS173 (
  input  GND,
  input  VCC,
  input  OE1,
  input  OE2,
  input  D1,
  input  IE1,
  input  IE2,
  input  D2,
  input  CLK,
  input  D3,
  input  D4,
  input  CLR,
  output Q1,
  output Q2,
  output Q3,
  output Q4
);

  wire and_1_out, and_2_out, and_3_out, and_4_out, and_5_out, and_6_out, and_7_out, and_8_out, and_9_out,
       and_10_out, d_ff_1_q, d_ff_1_qn, d_ff_2_q, d_ff_2_qn, d_ff_3_q, d_ff_3_qn, d_ff_4_q, d_ff_4_qn,
       not_1_out, not_2_out, not_3_out, not_4_out, not_5_out, not_6_out, not_7_out, not_8_out, not_9_out,
       not_10_out, or_1_out, or_2_out, or_3_out, or_4_out;

  not not_1 (not_1_out, OE1);
  and and_1 (and_1_out, not_1_out, not_2_out);
  not not_2 (not_2_out, OE2);
  not not_3 (not_3_out, IE1);
  and and_2 (and_2_out, not_3_out, not_4_out);
  not not_4 (not_4_out, IE2);
  not not_5 (not_5_out, CLK);
  not not_6 (not_6_out, and_2_out);
  and and_3 (and_3_out, d_ff_1_q, not_6_out);
  and and_4 (and_4_out, D1, and_2_out);
  and and_5 (and_5_out, d_ff_2_q, not_6_out);
  and and_6 (and_6_out, D2, and_2_out);
  and and_7 (and_7_out, d_ff_3_q, not_6_out);
  and and_8 (and_8_out, D3, and_2_out);
  and and_9 (and_9_out, d_ff_4_q, not_6_out);
  and and_10 (and_10_out, D4, and_2_out);
  D_Flip_Flop d_ff_1 (.D(or_1_out), .clk(not_7_out), .Q(d_ff_1_q), .Qn(d_ff_1_qn), .reset(CLR));  // open: preset
  or or_1 (or_1_out, and_3_out, and_4_out);
  not not_7 (not_7_out, not_5_out);
  D_Flip_Flop d_ff_2 (.D(or_2_out), .clk(not_8_out), .Q(d_ff_2_q), .Qn(d_ff_2_qn), .reset(CLR));  // open: preset
  or or_2 (or_2_out, and_5_out, and_6_out);
  not not_8 (not_8_out, not_5_out);
  D_Flip_Flop d_ff_3 (.D(or_3_out), .clk(not_9_out), .Q(d_ff_3_q), .Qn(d_ff_3_qn), .reset(CLR));  // open: preset
  or or_3 (or_3_out, and_7_out, and_8_out);
  not not_9 (not_9_out, not_5_out);
  D_Flip_Flop d_ff_4 (.D(or_4_out), .clk(not_10_out), .Q(d_ff_4_q), .Qn(d_ff_4_qn), .reset(CLR));  // open: preset
  or or_4 (or_4_out, and_9_out, and_10_out);
  not not_10 (not_10_out, not_5_out);
  assign Q1 = and_1_out ? ~d_ff_1_qn : 1'bz;  // Controlled_Inverter controlled_inverter_1
  assign Q2 = and_1_out ? ~d_ff_2_qn : 1'bz;  // Controlled_Inverter controlled_inverter_2
  assign Q3 = and_1_out ? ~d_ff_3_qn : 1'bz;  // Controlled_Inverter controlled_inverter_3
  assign Q4 = and_1_out ? ~d_ff_4_qn : 1'bz;  // Controlled_Inverter controlled_inverter_4
endmodule
