// Logisim project 74LS191.circ as structural Verilog: 2 circuits, main circuit IC_74LS191
module IC_74LS191 (
  input  CLK,
  input  DOWN_UP,
  input  A,
  input  ENABLE_G,
  input  B,
  input  C,
  input  D,
  input  LOAD,
  output RIPPLE_CLOCK,
  output MAX_MIN,
  output QA,
  output QB,
  output QC,
  output QD
);

  wire and_1_out, and_2_out, and_3_out, and_4_out, and_5_out, and_6_out, and_7_out, and_8_out, and_9_out,
       and_10_out, l_jk_nclk_ns_nr_f794c4de_1_q_n, l_jk_nclk_ns_nr_f794c4de_2_q_n,
       l_jk_nclk_ns_nr_f794c4de_3_q_n, l_jk_nclk_ns_nr_f794c4de_4_q_n, nand_1_out, nand_2_out, nand_3_out,
       nand_4_out, nand_5_out, nand_6_out, nand_7_out, nand_8_out, not_1_out, not_2_out, not_3_out,
       not_4_out, not_5_out, or_2_out, or_3_out, or_4_out;

  not not_1 (not_1_out, CLK);
  not not_2 (not_2_out, DOWN_UP);
  not not_3 (not_3_out, LOAD);
  not not_4 (not_4_out, not_2_out);
  and and_1 (and_1_out, ~not_4_out, ~ENABLE_G);  // AND_Gate
  and and_2 (and_2_out, ~ENABLE_G, ~not_2_out);  // AND_Gate
  and and_3 (and_3_out, QA, QC);
  and and_4 (and_4_out, l_jk_nclk_ns_nr_f794c4de_1_q_n, l_jk_nclk_ns_nr_f794c4de_3_q_n);
  nand nand_1 (nand_1_out, A, not_3_out);
  not not_5 (not_5_out, ENABLE_G);
  nand nand_2 (nand_2_out, B, not_3_out);
  and and_5 (and_5_out, and_2_out, l_jk_nclk_ns_nr_f794c4de_1_q_n);
  and and_6 (and_6_out, QA, and_1_out);
  nand nand_3 (nand_3_out, C, not_3_out);
  and and_7 (and_7_out, and_2_out, l_jk_nclk_ns_nr_f794c4de_1_q_n, l_jk_nclk_ns_nr_f794c4de_2_q_n);
  and and_8 (and_8_out, QA, QB, and_1_out);
  nand nand_4 (nand_4_out, D, not_3_out);
  and and_9 (and_9_out, and_2_out, l_jk_nclk_ns_nr_f794c4de_1_q_n, l_jk_nclk_ns_nr_f794c4de_2_q_n, l_jk_nclk_ns_nr_f794c4de_3_q_n);
  and and_10 (and_10_out, QA, QB, QC, and_1_out);
  or or_1 (MAX_MIN, and_3_out, and_4_out);
  nand nand_5 (nand_5_out, nand_1_out, not_3_out);
  or or_2 (or_2_out, and_5_out, and_6_out);
  nand nand_6 (nand_6_out, nand_2_out, not_3_out);
  or or_3 (or_3_out, and_7_out, and_8_out);
  nand nand_7 (nand_7_out, nand_3_out, not_3_out);
  or or_4 (or_4_out, and_9_out, and_10_out);
  nand nand_8 (nand_8_out, nand_4_out, not_3_out);
  nand nand_9 (RIPPLE_CLOCK, not_1_out, not_5_out, MAX_MIN);
  L_JK_nCLK_nS_nR_f794c4de l_jk_nclk_ns_nr_f794c4de_1 (
    .J(not_5_out), .K(not_5_out), .CLK(not_1_out), .SET(nand_1_out), .L_R_ce9ba302(nand_5_out), .Q(QA),
    .Q_N(l_jk_nclk_ns_nr_f794c4de_1_q_n));
  L_JK_nCLK_nS_nR_f794c4de l_jk_nclk_ns_nr_f794c4de_2 (
    .J(or_2_out), .K(or_2_out), .CLK(not_1_out), .SET(nand_2_out), .L_R_ce9ba302(nand_6_out), .Q(QB),
    .Q_N(l_jk_nclk_ns_nr_f794c4de_2_q_n));
  L_JK_nCLK_nS_nR_f794c4de l_jk_nclk_ns_nr_f794c4de_3 (
    .J(or_3_out), .K(or_3_out), .CLK(not_1_out), .SET(nand_3_out), .L_R_ce9ba302(nand_7_out), .Q(QC),
    .Q_N(l_jk_nclk_ns_nr_f794c4de_3_q_n));
  L_JK_nCLK_nS_nR_f794c4de l_jk_nclk_ns_nr_f794c4de_4 (
    .J(or_4_out), .K(or_4_out), .CLK(not_1_out), .SET(nand_4_out), .L_R_ce9ba302(nand_8_out), .Q(QD),
    .Q_N(l_jk_nclk_ns_nr_f794c4de_4_q_n));

  // Notes on the sheet:
  //   74LS191
endmodule

module L_JK_nCLK_nS_nR_f794c4de (
  input  SET,
  input  J,
  input  K,
  input  CLK,
  input  L_R_ce9ba302,
  output Q,
  output Q_N
);

  wire not_1_out, not_2_out;

  not not_1 (not_1_out, SET);
  J_K_Flip_Flop #(.trigger("falling")) Fall (
    .J(J), .K(K), .clk(CLK), .Q(Q), .Qn(Q_N), .preset(not_1_out), .reset(not_2_out));
  not not_2 (not_2_out, L_R_ce9ba302);
endmodule
