// Logisim project AS6C62256.circ as structural Verilog: 1 circuit, main circuit AS6C62256
module AS6C62256 (
  input  GND,
  input  VCC,
  input  A14,
  input  A13,
  input  A12,
  input  A11,
  input  A10,
  input  A9,
  input  A8,
  input  A7,
  input  A6,
  input  A5,
  input  A4,
  input  A3,
  input  A2,
  input  A1,
  input  A0,
  input  WE_N,
  input  D0_IN,
  input  CE_N,
  input  D1_IN,
  input  D2_IN,
  input  D3_IN,
  input  OE_N,
  input  D4_IN,
  input  D5_IN,
  input  D6_IN,
  input  D7_IN,
  output D0_OUT,
  output D1_OUT,
  output D2_OUT,
  output D3_OUT,
  output D4_OUT,
  output D5_OUT,
  output D6_OUT,
  output D7_OUT
);

  wire and_1_out, and_2_out, not_1_out, not_2_out, not_3_out;

  not not_1 (not_1_out, WE_N);
  not not_2 (not_2_out, CE_N);
  not not_3 (not_3_out, OE_N);
  and and_1 (and_1_out, not_1_out, not_2_out);
  and and_2 (and_2_out, not_2_out, not_3_out);
  RAM #(.addrWidth(15), .databus("bidir"), .trigger("high")) ram_1 (
    .addr({A14, A13, A12, A11, A10, A9, A8, A7, A6, A5, A4, A3, A2, A1, A0}), .we(and_1_out), .oe(and_2_out),
    .data({D7_IN, D6_IN, D5_IN, D4_IN, D3_IN, D2_IN, D1_IN, D0_IN}));
  assign {D7_OUT, D6_OUT, D5_OUT, D4_OUT, D3_OUT, D2_OUT, D1_OUT, D0_OUT} = and_2_out ? {D7_IN, D6_IN, D5_IN, D4_IN, D3_IN, D2_IN, D1_IN, D0_IN} : 8'bz;  // Controlled_Buffer controlled_buffer_1
endmodule
