// Logisim project breadboard_pc_v1.circ as structural Verilog: 3 circuits, main circuit main
module main (
  input  BUS_TEST_DIP_ENABLE,
  input  GLOBAL_CLEAR
);

  wire ALU_carry_out, ALU_negative_flag, ALU_overflow_flag, ALU_zero_flag, and_1_out, clock_1_out,
       FLAGS_REGISTER_q1, FLAGS_REGISTER_q2, FLAGS_REGISTER_q3, FLAGS_REGISTER_q4, not_1_out, not_2_out,
       not_3_out, not_4_out, not_5_out, not_6_out, not_7_out, not_8_out;
  wire [3:0] counter_1_q;
  wire [7:0] A_REGISTER_data_stored, ALU_alu_stored_output, B_REGISTER_data_stored, controlled_buffer_1_out,
       controlled_buffer_2_out, dipswitch_1_p8, INSTRUCTION_REGISTER_data_stored,
       MEMORY_ADRESS_REGISTER_data_out, MEMORY_ADRESS_REGISTER_data_stored, OPERAND_REGISTER_data_stored,
       OUTPUT_REGISTER_data_stored, PROGRAM_COUNTER_q;
  wire [11:0] OUTPUT_REGISTER_DECODER_data, PC_DECODER_data;
  wire [12:12] multiplexer_1_out;
  wire [23:0] MICROCODE_ROM_data;

  Clock clock_1 (.out(clock_1_out));
  not not_1 (not_1_out, clock_1_out);
  Counter #(.max('hf), .width(4)) counter_1 (
    .clr(GLOBAL_CLEAR), .load(MICROCODE_ROM_data[5]), .up(1'b1), .count(1'b1), .clk(not_1_out), .D(4'b0000),
    .Q(counter_1_q));  // open: carry
  ROM #(.addrWidth(13), .dataWidth(24)) MICROCODE_ROM (
    .addr({multiplexer_1_out[12], INSTRUCTION_REGISTER_data_stored, counter_1_q}), .data(MICROCODE_ROM_data));
  register_module INSTRUCTION_REGISTER (
    .INPUT_ENABLE(MICROCODE_ROM_data[17]), .DATA_IN(controlled_buffer_2_out), .OUTPUT_ENABLE(1'b1),
    .CLOCK(clock_1_out), .DATA_STORED(INSTRUCTION_REGISTER_data_stored));  // open: CLEAR, DATA_OUT
  LedBar ledbar_1 (
    .led0(INSTRUCTION_REGISTER_data_stored[7]), .led1(INSTRUCTION_REGISTER_data_stored[6]),
    .led2(INSTRUCTION_REGISTER_data_stored[5]), .led3(INSTRUCTION_REGISTER_data_stored[4]),
    .led4(INSTRUCTION_REGISTER_data_stored[3]), .led5(INSTRUCTION_REGISTER_data_stored[2]),
    .led6(INSTRUCTION_REGISTER_data_stored[1]), .led7(INSTRUCTION_REGISTER_data_stored[0]));
  not not_2 (not_2_out, MICROCODE_ROM_data[4]);
  Multiplexer #(.select(2)) multiplexer_1 (
    .in0(FLAGS_REGISTER_q4), .in1(FLAGS_REGISTER_q3), .in2(FLAGS_REGISTER_q2), .in3(FLAGS_REGISTER_q1),
    .out(multiplexer_1_out[12]),
    .sel({INSTRUCTION_REGISTER_data_stored[0], INSTRUCTION_REGISTER_data_stored[1]}));
  and and_1 (and_1_out, not_2_out, clock_1_out);
  IC74LS173 FLAGS_REGISTER (
    .OE1(1'b0), .OE2(1'b0), .D1(ALU_carry_out), .IE1(1'b0), .IE2(1'b0), .D2(ALU_zero_flag), .CLK(and_1_out),
    .D3(ALU_negative_flag), .D4(ALU_overflow_flag), .CLR(1'b0), .Q1(FLAGS_REGISTER_q1),
    .Q2(FLAGS_REGISTER_q2), .Q3(FLAGS_REGISTER_q3), .Q4(FLAGS_REGISTER_q4));  // open: GND, VCC
  not not_3 (not_3_out, MICROCODE_ROM_data[18]);
  not not_4 (not_4_out, MICROCODE_ROM_data[19]);
  not not_5 (not_5_out, MICROCODE_ROM_data[22]);
  LedBar ledbar_2 (
    .led0(controlled_buffer_2_out[7]), .led1(controlled_buffer_2_out[6]), .led2(controlled_buffer_2_out[5]),
    .led3(controlled_buffer_2_out[4]), .led4(controlled_buffer_2_out[3]), .led5(controlled_buffer_2_out[2]),
    .led6(controlled_buffer_2_out[1]), .led7(controlled_buffer_2_out[0]));
  assign controlled_buffer_1_out = not_3_out ? controlled_buffer_2_out : 8'bz;  // Controlled_Buffer controlled_buffer_1
  assign controlled_buffer_2_out = not_4_out ? controlled_buffer_1_out : 8'bz;  // Controlled_Buffer controlled_buffer_2
  not not_6 (not_6_out, MICROCODE_ROM_data[23]);
  assign controlled_buffer_2_out = not_6_out ? PROGRAM_COUNTER_q : 8'bz;  // Controlled_Buffer controlled_buffer_3
  not not_7 (not_7_out, MICROCODE_ROM_data[6]);
  assign controlled_buffer_2_out = BUS_TEST_DIP_ENABLE ? dipswitch_1_p8 : 8'bz;  // Controlled_Buffer controlled_buffer_4
  RAM #(.asyncread("true"), .clearpin("true"), .databus("bidir"), .\type ("nonvolatile")) RAM_MODULE (
    .addr(MEMORY_ADRESS_REGISTER_data_stored), .we(not_3_out), .oe(not_8_out), .clk(and_1_out),
    .data(controlled_buffer_1_out));  // open: clr
  not not_8 (not_8_out, not_3_out);
  Counter PROGRAM_COUNTER (
    .clr(GLOBAL_CLEAR), .load(not_5_out), .up(1'b1), .count(MICROCODE_ROM_data[21]), .clk(and_1_out),
    .D(controlled_buffer_2_out), .Q(PROGRAM_COUNTER_q));  // open: carry
  // DipSwitch dipswitch_1: pin names not known; wires that end beside it: dipswitch_1_p8[7], dipswitch_1_p8[6], dipswitch_1_p8[5], dipswitch_1_p8[4], dipswitch_1_p8[3], dipswitch_1_p8[2], dipswitch_1_p8[1], dipswitch_1_p8[0]
  register_module A_REGISTER (
    .CLEAR(GLOBAL_CLEAR), .INPUT_ENABLE(MICROCODE_ROM_data[14]), .DATA_IN(controlled_buffer_2_out),
    .OUTPUT_ENABLE(MICROCODE_ROM_data[13]), .CLOCK(and_1_out), .DATA_STORED(A_REGISTER_data_stored),
    .DATA_OUT(controlled_buffer_2_out));
  register_module B_REGISTER (
    .CLEAR(GLOBAL_CLEAR), .INPUT_ENABLE(MICROCODE_ROM_data[12]), .DATA_IN(controlled_buffer_2_out),
    .OUTPUT_ENABLE(MICROCODE_ROM_data[11]), .CLOCK(and_1_out), .DATA_STORED(B_REGISTER_data_stored),
    .DATA_OUT(controlled_buffer_2_out));
  alu_module ALU (
    .ALU_OP0(MICROCODE_ROM_data[10]), .ALU_OP1(MICROCODE_ROM_data[9]), .ALU_OE_N(MICROCODE_ROM_data[7]),
    .B_INPUT(B_REGISTER_data_stored), .SUB_SIGNAL(MICROCODE_ROM_data[8]), .A_INPUT(A_REGISTER_data_stored),
    .OVERFLOW_FLAG(ALU_overflow_flag), .ZERO_FLAG(ALU_zero_flag), .NEGATIVE_FLAG(ALU_negative_flag),
    .ALU_OUTPUT(controlled_buffer_2_out), .CARRY_OUT(ALU_carry_out), .ALU_STORED_OUTPUT(ALU_alu_stored_output));
  register_module MEMORY_ADRESS_REGISTER (
    .CLEAR(GLOBAL_CLEAR), .INPUT_ENABLE(MICROCODE_ROM_data[20]), .DATA_IN(controlled_buffer_2_out),
    .OUTPUT_ENABLE(1'b0), .CLOCK(and_1_out), .DATA_STORED(MEMORY_ADRESS_REGISTER_data_stored),
    .DATA_OUT(MEMORY_ADRESS_REGISTER_data_out));
  register_module OPERAND_REGISTER (
    .CLEAR(GLOBAL_CLEAR), .INPUT_ENABLE(MICROCODE_ROM_data[16]), .DATA_IN(controlled_buffer_2_out),
    .OUTPUT_ENABLE(MICROCODE_ROM_data[15]), .CLOCK(and_1_out), .DATA_STORED(OPERAND_REGISTER_data_stored),
    .DATA_OUT(controlled_buffer_2_out));
  register_module OUTPUT_REGISTER (
    .CLEAR(1'b0), .INPUT_ENABLE(not_7_out), .DATA_IN(controlled_buffer_2_out), .OUTPUT_ENABLE(1'b0),
    .CLOCK(and_1_out), .DATA_STORED(OUTPUT_REGISTER_data_stored));  // open: DATA_OUT
  LedBar ledbar_3 (
    .led0(A_REGISTER_data_stored[7]), .led1(A_REGISTER_data_stored[6]), .led2(A_REGISTER_data_stored[5]),
    .led3(A_REGISTER_data_stored[4]), .led4(A_REGISTER_data_stored[3]), .led5(A_REGISTER_data_stored[2]),
    .led6(A_REGISTER_data_stored[1]), .led7(A_REGISTER_data_stored[0]));
  LedBar ledbar_4 (
    .led0(B_REGISTER_data_stored[7]), .led1(B_REGISTER_data_stored[6]), .led2(B_REGISTER_data_stored[5]),
    .led3(B_REGISTER_data_stored[4]), .led4(B_REGISTER_data_stored[3]), .led5(B_REGISTER_data_stored[2]),
    .led6(B_REGISTER_data_stored[1]), .led7(B_REGISTER_data_stored[0]));
  ROM #(.dataWidth(12)) PC_DECODER (.addr(PROGRAM_COUNTER_q), .data(PC_DECODER_data));
  ROM #(.dataWidth(12)) OUTPUT_REGISTER_DECODER (
    .addr(OUTPUT_REGISTER_data_stored), .data(OUTPUT_REGISTER_DECODER_data));
  LedBar ledbar_5 (
    .led0(ALU_alu_stored_output[7]), .led1(ALU_alu_stored_output[6]), .led2(ALU_alu_stored_output[5]),
    .led3(ALU_alu_stored_output[4]), .led4(ALU_alu_stored_output[3]), .led5(ALU_alu_stored_output[2]),
    .led6(ALU_alu_stored_output[1]), .led7(ALU_alu_stored_output[0]));
  LedBar ledbar_6 (
    .led0(MEMORY_ADRESS_REGISTER_data_stored[7]), .led1(MEMORY_ADRESS_REGISTER_data_stored[6]),
    .led2(MEMORY_ADRESS_REGISTER_data_stored[5]), .led3(MEMORY_ADRESS_REGISTER_data_stored[4]),
    .led4(MEMORY_ADRESS_REGISTER_data_stored[3]), .led5(MEMORY_ADRESS_REGISTER_data_stored[2]),
    .led6(MEMORY_ADRESS_REGISTER_data_stored[1]), .led7(MEMORY_ADRESS_REGISTER_data_stored[0]));
  LedBar ledbar_7 (
    .led0(controlled_buffer_1_out[7]), .led1(controlled_buffer_1_out[6]), .led2(controlled_buffer_1_out[5]),
    .led3(controlled_buffer_1_out[4]), .led4(controlled_buffer_1_out[3]), .led5(controlled_buffer_1_out[2]),
    .led6(controlled_buffer_1_out[1]), .led7(controlled_buffer_1_out[0]));
  LedBar ledbar_8 (
    .led0(OPERAND_REGISTER_data_stored[7]), .led1(OPERAND_REGISTER_data_stored[6]),
    .led2(OPERAND_REGISTER_data_stored[5]), .led3(OPERAND_REGISTER_data_stored[4]),
    .led4(OPERAND_REGISTER_data_stored[3]), .led5(OPERAND_REGISTER_data_stored[2]),
    .led6(OPERAND_REGISTER_data_stored[1]), .led7(OPERAND_REGISTER_data_stored[0]));
  Hex_Digit_Display #(.decimalPoint("false")) hex_digit_display_1 (.value(PC_DECODER_data[11:8]));
  Hex_Digit_Display #(.decimalPoint("false")) hex_digit_display_2 (.value(OUTPUT_REGISTER_DECODER_data[11:8]));
  Hex_Digit_Display #(.decimalPoint("false")) hex_digit_display_3 (.value(PC_DECODER_data[7:4]));
  Hex_Digit_Display #(.decimalPoint("false")) hex_digit_display_4 (.value(PC_DECODER_data[3:0]));
  Hex_Digit_Display #(.decimalPoint("false")) hex_digit_display_5 (.value(OUTPUT_REGISTER_DECODER_data[7:4]));
  Hex_Digit_Display #(.decimalPoint("false")) hex_digit_display_6 (.value(OUTPUT_REGISTER_DECODER_data[3:0]));

  // Notes on the sheet:
  //   Inverted Clock
  //   contents of MICROCODE_ROM (hex, n*v repeats v):
  //   4ff880 f5f880 4ff880 f6f880 dff8a0 11*dff890 4ff880 f5f880 4ff880 f6f880 cf7880 d7b8a0 10*dff890
  //   4ff880 f5f880 4ff880 f6f880 cf7880 d7e8a0 10*dff890 4ff880 f5f880 4ff880 f6f880 dfb820 11*dff890
  //   4ff880 f5f880 4ff880 f6f880 dfb920 11*dff890 4ff880 f5f880 4ff880 f6f880 df38a0 11*dff890 4ff880
  //   f5f880 4ff880 f6f880 df68a0 11*dff890 4ff880 f5f880 4ff880 f6f880 dfd8e0 11*dff890 4ff880 f5f880
  //   4ff880 f6f880 9f78a0 11*dff890 4ff880 f5f880 4ff880 f6f880 dfba20 11*dff890 4ff880 f5f880 4ff880
  //   f6f880 dfbe20 11*dff890 4ff880 f5f880 4ff880 f6f880 dfbc20 11*dff890 4ff880 f5f880 4ff880 f6f880
  //   cf7880 dbd8a0 10*dff890 4ff880 f5f880 4ff880 f6f880 cf7880 dbf0a0 10*dff890 4ff880 f5f880 4ff880
  //   f6f880 12*dff890 4ff880 f5f880 4ff880 f6f880 df6880 dfb820 10*dff890 4ff880 f5f880 4ff880 f6f880
  //   12*dff890 4ff880 f5f880 4ff880 f6f880 12*dff890 4ff880 f5f880 4ff880 f6f880 12*dff890 4ff880 f5f880
  //   4ff880 f6f880 12*dff890 4ff880 f5f880 4ff880 f6f880 12*dff890 4ff880 f5f880 4ff880 f6f880 12*dff890
  //   4ff880 f5f880 4ff880 f6f880 12*dff890 4ff880 f5f880 4ff880 f6f880 12*dff890 4ff880 f5f880 4ff880
  //   f6f880 12*dff890 4ff880 f5f880 4ff880 f6f880 12*dff890 4ff880 f5f880 4ff880 f6f880 12*dff890 4ff880
  //   f5f880 4ff880 f6f880 12*dff890 4ff880 f5f880 4ff880 f6f880 12*dff890 4ff880 f5f880 4ff880 f6f880
  //   12*dff890 4ff880 f5f880 4ff880 f6f880 12*dff890 4ff880 f5f880 4ff880 f6f880 12*dff890 4ff880 f5f880
  //   4ff880 f6f880 12*dff890 4ff880 f5f880 4ff880 f6f880 12*dff890 4ff880 f5f880 4ff880 f6f880 12*dff890
  //   4ff880 f5f880 4ff880 f6f880 12*dff890 4ff880 f5f880 4ff880 f6f880 12*dff890 4ff880 f5f880 4ff880
  //   f6f880 12*dff890 4ff880 f5f880 4ff880 f6f880 12*dff890 4ff880 f5f880 4ff880 f6f880 12*dff890 4ff880
  //   f5f880 4ff880 f6f880 12*dff890 4ff880 f5f880 4ff880 f6f880 12*dff890 4ff880 f5f880 4ff880 f6f880
  //   12*dff890 4ff880 f5f880 4ff880 f6f880 12*dff890 4ff880 f5f880 4ff880 f6f880 12*dff890 4ff880 f5f880
  //   4ff880 f6f880 12*dff890 4ff880 f5f880 4ff880 f6f880 12*dff890 4ff880 f5f880 4ff880 f6f880 12*dff890
  //   4ff880 f5f880 4ff880 f6f880 12*dff890 4ff880 f5f880 4ff880 f6f880 12*dff890 4ff880 f5f880 4ff880
  //   f6f880 12*dff890 4ff880 f5f880 4ff880 f6f880 12*dff890 4ff880 f5f880 4ff880 f6f880 12*dff890 4ff880
  //   f5f880 4ff880 f6f880 12*dff890 4ff880 f5f880 4ff880 f6f880 12*dff890 4ff880 f5f880 4ff880 f6f880
  //   12*dff890 4ff880 f5f880 4ff880 f6f880 12*dff890 4ff880 f5f880 4ff880 f6f880 12*dff890 4ff880 f5f880
  //   4ff880 f6f880 12*dff890 4ff880 f5f880 4ff880 f6f880 12*dff890 4ff880 f5f880 4ff880 f6f880 12*dff890
  //   4ff880 f5f880 4ff880 f6f880 12*dff890 4ff880 f5f880 4ff880 f6f880 12*dff890 4ff880 f5f880 4ff880
  //   f6f880 12*dff890 4ff880 f5f880 4ff880 f6f880 12*dff890 4ff880 f5f880 4ff880 f6f880 12*dff890 4ff880
  //   f5f880 4ff880 f6f880 12*dff890 4ff880 f5f880 4ff880 f6f880 12*dff890 4ff880 f5f880 4ff880 f6f880
  //   12*dff890 4ff880 f5f880 4ff880 f6f880 12*dff890 4ff880 f5f880 4ff880 f6f880 12*dff890 4ff880 f5f880
  //   4ff880 f6f880 12*dff890 4ff880 f5f880 4ff880 f6f880 12*dff890 4ff880 f5f880 4ff880 f6f880 12*dff890
  //   4ff880 f5f880 4ff880 f6f880 12*dff890 4ff880 f5f880 4ff880 f6f880 12*dff890 4ff880 f5f880 4ff880
  //   f6f880 12*dff890 4ff880 f5f880 4ff880 f6f880 12*dff890 4ff880 f5f880 4ff880 f6f880 12*dff890 4ff880
  //   f5f880 4ff880 f6f880 12*dff890 4ff880 f5f880 4ff880 f6f880 12*dff890 4ff880 f5f880 4ff880 f6f880
  //   12*dff890 4ff880 f5f880 4ff880 f6f880 12*dff890 4ff880 f5f880 4ff880 f6f880 12*dff890 4ff880 f5f880
  //   4ff880 f6f880 12*dff890 4ff880 f5f880 4ff880 f6f880 12*dff890 4ff880 f5f880 4ff880 f6f880 12*dff890
  //   4ff880 f5f880 4ff880 f6f880 12*dff890 4ff880 f5f880 4ff880 f6f880 12*dff890 4ff880 f5f880 4ff880
  //   f6f880 12*dff890 4ff880 f5f880 4ff880 f6f880 12*dff890 4ff880 f5f880 4ff880 f6f880 12*dff890 4ff880
  //   f5f880 4ff880 f6f880 12*dff890 4ff880 f5f880 4ff880 f6f880 12*dff890 4ff880 f5f880 4ff880 f6f880
  //   12*dff890 4ff880 f5f880 4ff880 f6f880 12*dff890 4ff880 f5f880 4ff880 f6f880 12*dff890 4ff880 f5f880
  //   4ff880 f6f880 12*dff890 4ff880 f5f880 4ff880 f6f880 12*dff890 4ff880 f5f880 4ff880 f6f880 12*dff890
  //   4ff880 f5f880 4ff880 f6f880 12*dff890 4ff880 f5f880 4ff880 f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
  //   UNUSED
  //   UNUSED
  //   UNUSED
  //   UNUSED
  //   HALT
  //   END
  //   OUT_IE
  //   ALU_OE_N
  //   ALU_SUB
  //   ALU_OP1
  //   ALU_OP0
  //   B_REG_OE_N
  //   B_REG_IE_N
  //   A_REG_OE_N
  //   A_REG_IE_N
  //   OPR_OE_N
  //   OPR_IE_N
  //   IR_IE_N
  //   RAM_WE_N
  //   RAM_OE_N
  //   MAR_IE_N
  //   PC_INCREMENT
  //   PC_LOAD_N
  //   PC_OE_N
  //   00 - ADD/SUB
  //   01 - AND
  //   10 - XOR
  //   11 - OR
  //   ALU_CARRY
  //   ALU_NEGATIVE
  //   ALU_ZERO
  //   ALU_OVERFLOW
  //   contents of PC_DECODER (hex, n*v repeats v):
  //   0 1 2 3 4 5 6 7 8 9 10 11 12 13 14 15 16 17 18 19 20 21 22 23 24 25 26 27 28 29 30 31 32 33 34 35 36
  //   37 38 39 40 41 42 43 44 45 46 47 48 49 50 51 52 53 54 55 56 57 58 59 60 61 62 63 64 65 66 67 68 69
  //   70 71 72 73 74 75 76 77 78 79 80 81 82 83 84 85 86 87 88 89 90 91 92 93 94 95 96 97 98 99 100 101
  //   102 103 104 105 106 107 108 109 110 111 112 113 114 115 116 117 118 119 120 121 122 123 124 125 126
  //   127 128 129 130 131 132 133 134 135 136 137 138 139 140 141 142 143 144 145 146 147 148 149 150 151
  //   152 153 154 155 156 157 158 159 160 161 162 163 164 165 166 167 168 169 170 171 172 173 174 175 176
  //   177 178 179 180 181 182 183 184 185 186 187 188 189 190 191 192 193 194 195 196 197 198 199 200 201
  //   202 203 204 205 206 207 208 209 210 211 212 213 214 215 216 217 218 219 220 221 222 223 224 225 226
  //   227 228 229 230 231 232 233 234 235 236 237 238 239 240 241 242 243 244 245 246 247 248 249 250 251
  //   252 253 254 255
  //   contents of OUTPUT_REGISTER_DECODER (hex, n*v repeats v):
  //   0 1 2 3 4 5 6 7 8 9 10 11 12 13 14 15 16 17 18 19 20 21 22 23 24 25 26 27 28 29 30 31 32 33 34 35 36
  //   37 38 39 40 41 42 43 44 45 46 47 48 49 50 51 52 53 54 55 56 57 58 59 60 61 62 63 64 65 66 67 68 69
  //   70 71 72 73 74 75 76 77 78 79 80 81 82 83 84 85 86 87 88 89 90 91 92 93 94 95 96 97 98 99 100 101
  //   102 103 104 105 106 107 108 109 110 111 112 113 114 115 116 117 118 119 120 121 122 123 124 125 126
  //   127 128 129 130 131 132 133 134 135 136 137 138 139 140 141 142 143 144 145 146 147 148 149 150 151
  //   152 153 154 155 156 157 158 159 160 161 162 163 164 165 166 167 168 169 170 171 172 173 174 175 176
  //   177 178 179 180 181 182 183 184 185 186 187 188 189 190 191 192 193 194 195 196 197 198 199 200 201
  //   202 203 204 205 206 207 208 209 210 211 212 213 214 215 216 217 218 219 220 221 222 223 224 225 226
  //   227 228 229 230 231 232 233 234 235 236 237 238 239 240 241 242 243 244 245 246 247 248 249 250 251
  //   252 253 254 255
endmodule

module register_module (
  input  CLEAR,
  input  INPUT_ENABLE,
  input  [7:0] DATA_IN,
  input  OUTPUT_ENABLE,
  input  CLOCK,
  output [7:0] DATA_STORED,
  output [7:0] DATA_OUT
);

  wire n74245_1_pin1;

  _74245 u_74245_1 (
    .pin1(n74245_1_pin1), .pin2(DATA_STORED[7]), .pin3(DATA_STORED[6]), .pin4(DATA_STORED[5]),
    .pin5(DATA_STORED[4]), .pin6(DATA_STORED[3]), .pin7(DATA_STORED[2]), .pin8(DATA_STORED[1]),
    .pin9(DATA_STORED[0]), .pin19(OUTPUT_ENABLE), .pin18(DATA_OUT[7]), .pin17(DATA_OUT[6]),
    .pin16(DATA_OUT[5]), .pin15(DATA_OUT[4]), .pin14(DATA_OUT[3]), .pin13(DATA_OUT[2]), .pin12(DATA_OUT[1]),
    .pin11(DATA_OUT[0]));
  IC74LS173 ic74ls173_1 (
    .OE1(1'b0), .OE2(1'b0), .D1(DATA_IN[0]), .IE1(INPUT_ENABLE), .IE2(INPUT_ENABLE), .D2(DATA_IN[1]),
    .CLK(CLOCK), .D3(DATA_IN[2]), .D4(DATA_IN[3]), .CLR(CLEAR), .Q1(DATA_STORED[0]), .Q2(DATA_STORED[1]),
    .Q3(DATA_STORED[2]), .Q4(DATA_STORED[3]));  // open: GND, VCC
  IC74LS173 ic74ls173_2 (
    .OE1(1'b0), .OE2(1'b0), .D1(DATA_IN[4]), .IE1(INPUT_ENABLE), .IE2(INPUT_ENABLE), .D2(DATA_IN[5]),
    .CLK(CLOCK), .D3(DATA_IN[6]), .D4(DATA_IN[7]), .CLR(CLEAR), .Q1(DATA_STORED[4]), .Q2(DATA_STORED[5]),
    .Q3(DATA_STORED[6]), .Q4(DATA_STORED[7]));  // open: GND, VCC
  // also tied to VCC on the sheet: n74245_1_pin1
endmodule

module alu_module (
  input  ALU_OP0,
  input  ALU_OP1,
  input  ALU_OE_N,
  input  [7:0] B_INPUT,
  input  SUB_SIGNAL,
  input  [7:0] A_INPUT,
  output OVERFLOW_FLAG,
  output ZERO_FLAG,
  output NEGATIVE_FLAG,
  output [7:0] ALU_OUTPUT,
  output CARRY_OUT,
  output [7:0] ALU_STORED_OUTPUT
);

  wire not_1_out, not_2_out, xor_17_out, xor_18_out;
  wire [7:0] adder_1_out, and_1_out, multiplexer_1_out, multiplexer_2_out, or_1_out, xor_1_out, xor_9_out;

  LedBar A_INPUT_BAR (
    .led0(A_INPUT[7]), .led1(A_INPUT[6]), .led2(A_INPUT[5]), .led3(A_INPUT[4]), .led4(A_INPUT[3]),
    .led5(A_INPUT[2]), .led6(A_INPUT[1]), .led7(A_INPUT[0]));
  LedBar B_INPUT_BAR (
    .led0(B_INPUT[7]), .led1(B_INPUT[6]), .led2(B_INPUT[5]), .led3(B_INPUT[4]), .led4(B_INPUT[3]),
    .led5(B_INPUT[2]), .led6(B_INPUT[1]), .led7(B_INPUT[0]));
  xor xor_1 (xor_1_out[0], B_INPUT[0], SUB_SIGNAL);
  xor xor_2 (xor_1_out[1], B_INPUT[1], SUB_SIGNAL);
  xor xor_3 (xor_1_out[2], B_INPUT[2], SUB_SIGNAL);
  xor xor_4 (xor_1_out[3], B_INPUT[3], SUB_SIGNAL);
  xor xor_5 (xor_1_out[4], B_INPUT[4], SUB_SIGNAL);
  xor xor_6 (xor_1_out[5], B_INPUT[5], SUB_SIGNAL);
  xor xor_7 (xor_1_out[6], B_INPUT[6], SUB_SIGNAL);
  xor xor_8 (xor_1_out[7], B_INPUT[7], SUB_SIGNAL);
  xor xor_9 (xor_9_out[0], B_INPUT[0], A_INPUT[0]);
  xor xor_10 (xor_9_out[1], B_INPUT[1], A_INPUT[1]);
  xor xor_11 (xor_9_out[2], B_INPUT[2], A_INPUT[2]);
  xor xor_12 (xor_9_out[3], B_INPUT[3], A_INPUT[3]);
  xor xor_13 (xor_9_out[4], B_INPUT[4], A_INPUT[4]);
  xor xor_14 (xor_9_out[5], B_INPUT[5], A_INPUT[5]);
  xor xor_15 (xor_9_out[6], B_INPUT[6], A_INPUT[6]);
  xor xor_16 (xor_9_out[7], B_INPUT[7], A_INPUT[7]);
  and and_1 (and_1_out[0], B_INPUT[0], A_INPUT[0]);
  and and_2 (and_1_out[1], B_INPUT[1], A_INPUT[1]);
  and and_3 (and_1_out[2], B_INPUT[2], A_INPUT[2]);
  and and_4 (and_1_out[3], B_INPUT[3], A_INPUT[3]);
  and and_5 (and_1_out[4], B_INPUT[4], A_INPUT[4]);
  and and_6 (and_1_out[5], B_INPUT[5], A_INPUT[5]);
  and and_7 (and_1_out[6], B_INPUT[6], A_INPUT[6]);
  and and_8 (and_1_out[7], B_INPUT[7], A_INPUT[7]);
  or or_1 (or_1_out[0], B_INPUT[0], A_INPUT[0]);
  or or_2 (or_1_out[1], B_INPUT[1], A_INPUT[1]);
  or or_3 (or_1_out[2], B_INPUT[2], A_INPUT[2]);
  or or_4 (or_1_out[3], B_INPUT[3], A_INPUT[3]);
  or or_5 (or_1_out[4], B_INPUT[4], A_INPUT[4]);
  or or_6 (or_1_out[5], B_INPUT[5], A_INPUT[5]);
  or or_7 (or_1_out[6], B_INPUT[6], A_INPUT[6]);
  or or_8 (or_1_out[7], B_INPUT[7], A_INPUT[7]);
  LedBar ADDER_WORD_BAR (
    .led0(adder_1_out[7]), .led1(adder_1_out[6]), .led2(adder_1_out[5]), .led3(adder_1_out[4]),
    .led4(adder_1_out[3]), .led5(adder_1_out[2]), .led6(adder_1_out[1]), .led7(adder_1_out[0]));
  Adder adder_1 (.a(xor_1_out), .b(A_INPUT), .out(adder_1_out), .cin(SUB_SIGNAL), .cout(CARRY_OUT));
  LedBar XOR_WORD_BAR (
    .led0(xor_9_out[7]), .led1(xor_9_out[6]), .led2(xor_9_out[5]), .led3(xor_9_out[4]), .led4(xor_9_out[3]),
    .led5(xor_9_out[2]), .led6(xor_9_out[1]), .led7(xor_9_out[0]));
  LedBar AND_WORD_BAR (
    .led0(and_1_out[7]), .led1(and_1_out[6]), .led2(and_1_out[5]), .led3(and_1_out[4]), .led4(and_1_out[3]),
    .led5(and_1_out[2]), .led6(and_1_out[1]), .led7(and_1_out[0]));
  LedBar OR_WORD_BAR (
    .led0(or_1_out[7]), .led1(or_1_out[6]), .led2(or_1_out[5]), .led3(or_1_out[4]), .led4(or_1_out[3]),
    .led5(or_1_out[2]), .led6(or_1_out[1]), .led7(or_1_out[0]));
  xor xor_17 (xor_17_out, A_INPUT[7], xor_1_out[7]);
  xor xor_18 (xor_18_out, A_INPUT[7], ALU_STORED_OUTPUT[7]);
  not not_1 (not_1_out, xor_17_out);
  and and_9 (OVERFLOW_FLAG, not_1_out, xor_18_out);
  Multiplexer #(.width(8)) multiplexer_1 (.in0(adder_1_out), .in1(xor_9_out), .out(multiplexer_1_out), .sel(ALU_OP0));
  Multiplexer #(.width(8)) multiplexer_2 (.in0(and_1_out), .in1(or_1_out), .out(multiplexer_2_out), .sel(ALU_OP0));
  nor nor_1 (ZERO_FLAG, ALU_STORED_OUTPUT[0], ALU_STORED_OUTPUT[1], ALU_STORED_OUTPUT[2], ALU_STORED_OUTPUT[3], ALU_STORED_OUTPUT[4], ALU_STORED_OUTPUT[5], ALU_STORED_OUTPUT[6], ALU_STORED_OUTPUT[7]);
  Multiplexer #(.width(8)) multiplexer_3 (
    .in0(multiplexer_1_out), .in1(multiplexer_2_out), .out(ALU_STORED_OUTPUT), .sel(ALU_OP1));
  not not_2 (not_2_out, ALU_OE_N);
  assign ALU_OUTPUT = not_2_out ? ALU_STORED_OUTPUT : 8'bz;  // Controlled_Buffer controlled_buffer_1

  assign NEGATIVE_FLAG = ALU_STORED_OUTPUT[7];

  // Notes on the sheet:
  //   A7
  //   B7 xor SUB
  //   ADDER WORD
  //   XOR WORD
  //   AND WORD
  //   OR WORD
  //   Result7
  //   ADDER / XOR MUXED
  //   AND / OR MUXED
  //   00 - ADD/SUB
  //   01 - AND
  //   10 - XOR
  //   11 - OR
  //   FINAL MUXED OUTPUT
endmodule
