// Logisim project breadboard_pc_v6.circ as structural Verilog: 7 circuits, main circuit main
module main (
  input  BUS_TEST_DIP_ENABLE,
  input  GLOBAL_CLEAR
);

  wire ALU_carry_out, ALU_negative_flag, ALU_overflow_flag, ALU_zero_flag, and_1_out, CLK_out,
       FLAGS_REGISTER_q1, FLAGS_REGISTER_q2, FLAGS_REGISTER_q3, FLAGS_REGISTER_q4, not_1_out, not_3_out,
       not_4_out, not_5_out, not_6_out, not_7_out, not_8_out;
  wire [1:0] INSTRUCTION_REGISTER_data_stored;
  wire [3:0] counter_1_q, undriven_2;
  wire [7:0] A_REGISTER_data_stored, ALU_alu_stored_output, B_REGISTER_data_stored, CONTROL_LOGIC_ROM1_data,
       CONTROL_LOGIC_ROM2_data, CONTROL_LOGIC_ROM3_data, CONTROL_LOGIC_ROM4_data, controlled_buffer_1_out,
       controlled_buffer_3_out, dipswitch_1_p8, MEMORY_ADRESS_REGISTER_data_out,
       MEMORY_ADRESS_REGISTER_data_stored, OPERAND_REGISTER_data_stored, OUTPUT_REGISTER_data_stored,
       PROGRAM_COUNTER_REGISTER_p6, undriven, X_REGISTER_p8;
  wire [11:0] OUTPUT_REGISTER_DECODER_data, PC_DECODER_data;
  wire [12:6] INSTRUCTION_REGISTER_data_stored_2;
  wire [15:0] decoder_1_out0, not_2_out;
  wire [23:0] RAR_address_out;

  not not_1 (not_1_out, and_1_out);
  Counter #(.max('hf), .width(4)) counter_1 (
    .clr(GLOBAL_CLEAR), .load(CONTROL_LOGIC_ROM2_data[5]), .up(1'b1), .count(1'b1), .clk(not_1_out),
    .D(4'b0000), .Q(counter_1_q));  // open: carry
  Multiplexer #(.select(2)) multiplexer_1 (
    .in0(FLAGS_REGISTER_q1), .in1(FLAGS_REGISTER_q2), .in2(FLAGS_REGISTER_q3), .in3(FLAGS_REGISTER_q4),
    .out(INSTRUCTION_REGISTER_data_stored_2[12]), .sel(INSTRUCTION_REGISTER_data_stored));
  ROM #(.addrWidth(15)) CONTROL_LOGIC_ROM4 (
    .addr({2'b00, INSTRUCTION_REGISTER_data_stored_2, INSTRUCTION_REGISTER_data_stored, counter_1_q}),
    .data(CONTROL_LOGIC_ROM4_data));
  ROM #(.addrWidth(15)) CONTROL_LOGIC_ROM3 (
    .addr({2'b00, INSTRUCTION_REGISTER_data_stored_2, INSTRUCTION_REGISTER_data_stored, counter_1_q}),
    .data(CONTROL_LOGIC_ROM3_data));
  ROM #(.addrWidth(15)) CONTROL_LOGIC_ROM2 (
    .addr({2'b00, INSTRUCTION_REGISTER_data_stored_2, INSTRUCTION_REGISTER_data_stored, counter_1_q}),
    .data(CONTROL_LOGIC_ROM2_data));
  ROM #(.addrWidth(15)) CONTROL_LOGIC_ROM1 (
    .addr({2'b00, INSTRUCTION_REGISTER_data_stored_2, INSTRUCTION_REGISTER_data_stored, counter_1_q}),
    .data(CONTROL_LOGIC_ROM1_data));
  LED CARRY (.in(FLAGS_REGISTER_q1));
  LED ZERO (.in(FLAGS_REGISTER_q2));
  LED NEGATIVE (.in(FLAGS_REGISTER_q3));
  IC74LS173 FLAGS_REGISTER (
    .OE1(1'b0), .OE2(1'b0), .D1(ALU_carry_out), .IE1(CONTROL_LOGIC_ROM2_data[3]),
    .IE2(CONTROL_LOGIC_ROM2_data[3]), .D2(ALU_zero_flag), .CLK(and_1_out), .D3(ALU_negative_flag),
    .D4(ALU_overflow_flag), .CLR(1'b0), .Q1(FLAGS_REGISTER_q1), .Q2(FLAGS_REGISTER_q2),
    .Q3(FLAGS_REGISTER_q3), .Q4(FLAGS_REGISTER_q4));  // open: GND, VCC
  Decoder #(.enable("false"), .select(4)) decoder_1 (
    .out0(decoder_1_out0[0]), .out1(decoder_1_out0[1]), .out2(decoder_1_out0[2]), .out3(decoder_1_out0[3]),
    .out4(decoder_1_out0[4]), .out5(decoder_1_out0[5]), .out6(decoder_1_out0[6]), .out7(decoder_1_out0[7]),
    .out8(decoder_1_out0[8]), .out9(decoder_1_out0[9]), .out10(decoder_1_out0[10]),
    .out11(decoder_1_out0[11]), .out12(decoder_1_out0[12]), .out13(decoder_1_out0[13]),
    .out14(decoder_1_out0[14]), .out15(decoder_1_out0[15]), .sel(CONTROL_LOGIC_ROM1_data[3:0]));
  LED OVERFLOW (.in(FLAGS_REGISTER_q4));
  assign not_2_out = ~decoder_1_out0;  // NOT_Gate not_2, 16 bits wide
  register_module INSTRUCTION_REGISTER (
    .INPUT_ENABLE(CONTROL_LOGIC_ROM4_data[1]), .DATA_IN(controlled_buffer_1_out), .OUTPUT_ENABLE(1'b1),
    .CLOCK(and_1_out),
    .DATA_STORED({INSTRUCTION_REGISTER_data_stored_2[11:6], INSTRUCTION_REGISTER_data_stored}));  // open: CLEAR, DATA_OUT
  not not_3 (not_3_out, CONTROL_LOGIC_ROM4_data[2]);
  not not_4 (not_4_out, CONTROL_LOGIC_ROM4_data[3]);
  LedBar ledbar_1 (
    .led0(INSTRUCTION_REGISTER_data_stored_2[11]), .led1(INSTRUCTION_REGISTER_data_stored_2[10]),
    .led2(INSTRUCTION_REGISTER_data_stored_2[9]), .led3(INSTRUCTION_REGISTER_data_stored_2[8]),
    .led4(INSTRUCTION_REGISTER_data_stored_2[7]), .led5(INSTRUCTION_REGISTER_data_stored_2[6]),
    .led6(INSTRUCTION_REGISTER_data_stored[1]), .led7(INSTRUCTION_REGISTER_data_stored[0]));
  Clock CLK (.out(CLK_out));
  not not_5 (not_5_out, CONTROL_LOGIC_ROM2_data[4]);
  and and_1 (and_1_out, not_5_out, CLK_out);
  LedBar ledbar_2 (
    .led0(controlled_buffer_1_out[7]), .led1(controlled_buffer_1_out[6]), .led2(controlled_buffer_1_out[5]),
    .led3(controlled_buffer_1_out[4]), .led4(controlled_buffer_1_out[3]), .led5(controlled_buffer_1_out[2]),
    .led6(controlled_buffer_1_out[1]), .led7(controlled_buffer_1_out[0]));
  assign controlled_buffer_1_out = BUS_TEST_DIP_ENABLE ? dipswitch_1_p8 : 8'bz;  // Controlled_Buffer controlled_buffer_1
  not not_6 (not_6_out, and_1_out);
  // DipSwitch dipswitch_1: pin names not known; wires that end beside it: dipswitch_1_p8[7], dipswitch_1_p8[6], dipswitch_1_p8[5], dipswitch_1_p8[4], dipswitch_1_p8[3], dipswitch_1_p8[2], dipswitch_1_p8[1], dipswitch_1_p8[0]
  ROM_16MB_x_8 ROM_16MB (
    .OE_N(CONTROL_LOGIC_ROM1_data[4]), .RESET_N(not_6_out), .ADDRESS_IN(RAR_address_out),
    .DATA_OUT(controlled_buffer_1_out));
  ROM_ADDRESS_REGISTER RAR (
    .INCREMENT(CONTROL_LOGIC_ROM1_data[5]), .LOAD_S0(CONTROL_LOGIC_ROM1_data[6]),
    .LOAD_S1(CONTROL_LOGIC_ROM1_data[7]), .ADDRESS_IN(controlled_buffer_1_out), .CLK(and_1_out),
    .CLEAR(GLOBAL_CLEAR), .ADDRESS_OUT(RAR_address_out));
  VRAM_ADDRESS_REGISTER VRAR (
    .INCREMENT(not_2_out[1]), .LOAD_S0(not_2_out[2]), .LOAD_S1(not_2_out[3]));  // open: ADDRESS_IN, CLK, CLEAR, ADDRESS_OUT
  // counting_register_module PROGRAM_COUNTER_REGISTER: pin names not known; wires that end beside it: CONTROL_LOGIC_ROM4_data[5], CONTROL_LOGIC_ROM4_data[7], CONTROL_LOGIC_ROM4_data[6], GLOBAL_CLEAR, and_1_out, PROGRAM_COUNTER_REGISTER_p6, controlled_buffer_1_out, CONTROL_LOGIC_ROM2_data[0], CONTROL_LOGIC_ROM2_data[1]
  // counting_register_module X_REGISTER: pin names not known; wires that end beside it: controlled_buffer_1_out, CONTROL_LOGIC_ROM2_data[0], CONTROL_LOGIC_ROM2_data[1], CONTROL_LOGIC_ROM2_data[2], GLOBAL_CLEAR, and_1_out, controlled_buffer_1_out, X_REGISTER_p8
  Hex_Digit_Display #(.decimalPoint("false")) hex_digit_display_1 (.value(RAR_address_out[23:20]));
  Hex_Digit_Display #(.decimalPoint("false")) hex_digit_display_2 (.value(RAR_address_out[19:16]));
  assign controlled_buffer_1_out = not_4_out ? controlled_buffer_3_out : 8'bz;  // Controlled_Buffer controlled_buffer_2
  Hex_Digit_Display #(.decimalPoint("false")) hex_digit_display_3 (.value(RAR_address_out[15:12]));
  assign controlled_buffer_3_out = not_3_out ? controlled_buffer_1_out : 8'bz;  // Controlled_Buffer controlled_buffer_3
  not not_7 (not_7_out, CONTROL_LOGIC_ROM2_data[6]);
  Hex_Digit_Display #(.decimalPoint("false")) hex_digit_display_4 (.value(RAR_address_out[11:8]));
  Hex_Digit_Display #(.decimalPoint("false")) hex_digit_display_5 (.value(RAR_address_out[7:4]));
  RAM #(.asyncread("true"), .clearpin("true"), .databus("bidir"), .\type ("nonvolatile")) RAM_MODULE (
    .addr(MEMORY_ADRESS_REGISTER_data_stored), .we(not_3_out), .oe(not_8_out), .clk(and_1_out),
    .data(controlled_buffer_3_out));  // open: clr
  not not_8 (not_8_out, not_3_out);
  Hex_Digit_Display #(.decimalPoint("false")) hex_digit_display_6 (.value(RAR_address_out[3:0]));
  LedBar ledbar_3 (
    .led0(X_REGISTER_p8[7]), .led1(X_REGISTER_p8[6]), .led2(X_REGISTER_p8[5]), .led3(X_REGISTER_p8[4]),
    .led4(X_REGISTER_p8[3]), .led5(X_REGISTER_p8[2]), .led6(X_REGISTER_p8[1]), .led7(X_REGISTER_p8[0]));
  RAM #(.addrWidth(13)) ram_1 (.addr({1'b0, undriven_2, undriven}));  // open: we, oe, clk, din, dout
  register_module A_REGISTER (
    .CLEAR(GLOBAL_CLEAR), .INPUT_ENABLE(CONTROL_LOGIC_ROM3_data[6]), .DATA_IN(controlled_buffer_1_out),
    .OUTPUT_ENABLE(CONTROL_LOGIC_ROM3_data[5]), .CLOCK(and_1_out), .DATA_STORED(A_REGISTER_data_stored),
    .DATA_OUT(controlled_buffer_1_out));
  register_module B_REGISTER (
    .CLEAR(GLOBAL_CLEAR), .INPUT_ENABLE(CONTROL_LOGIC_ROM3_data[4]), .DATA_IN(controlled_buffer_1_out),
    .OUTPUT_ENABLE(CONTROL_LOGIC_ROM3_data[3]), .CLOCK(and_1_out), .DATA_STORED(B_REGISTER_data_stored),
    .DATA_OUT(controlled_buffer_1_out));
  alu_module ALU (
    .ALU_OP0(CONTROL_LOGIC_ROM3_data[2]), .ALU_OP1(CONTROL_LOGIC_ROM3_data[1]),
    .ALU_OE_N(CONTROL_LOGIC_ROM2_data[7]), .B_INPUT(B_REGISTER_data_stored),
    .SUB_SIGNAL(CONTROL_LOGIC_ROM3_data[0]), .A_INPUT(A_REGISTER_data_stored),
    .OVERFLOW_FLAG(ALU_overflow_flag), .ZERO_FLAG(ALU_zero_flag), .NEGATIVE_FLAG(ALU_negative_flag),
    .ALU_OUTPUT(controlled_buffer_1_out), .CARRY_OUT(ALU_carry_out), .ALU_STORED_OUTPUT(ALU_alu_stored_output));
  register_module MEMORY_ADRESS_REGISTER (
    .CLEAR(GLOBAL_CLEAR), .INPUT_ENABLE(CONTROL_LOGIC_ROM4_data[4]), .DATA_IN(controlled_buffer_1_out),
    .OUTPUT_ENABLE(1'b0), .CLOCK(and_1_out), .DATA_STORED(MEMORY_ADRESS_REGISTER_data_stored),
    .DATA_OUT(MEMORY_ADRESS_REGISTER_data_out));
  register_module OPERAND_REGISTER (
    .CLEAR(GLOBAL_CLEAR), .INPUT_ENABLE(CONTROL_LOGIC_ROM4_data[0]), .DATA_IN(controlled_buffer_1_out),
    .OUTPUT_ENABLE(CONTROL_LOGIC_ROM3_data[7]), .CLOCK(and_1_out),
    .DATA_STORED(OPERAND_REGISTER_data_stored), .DATA_OUT(controlled_buffer_1_out));
  register_module OUTPUT_REGISTER (
    .CLEAR(1'b0), .INPUT_ENABLE(not_7_out), .DATA_IN(controlled_buffer_1_out), .OUTPUT_ENABLE(1'b0),
    .CLOCK(and_1_out), .DATA_STORED(OUTPUT_REGISTER_data_stored));  // open: DATA_OUT
  LedBar ledbar_4 (
    .led0(A_REGISTER_data_stored[7]), .led1(A_REGISTER_data_stored[6]), .led2(A_REGISTER_data_stored[5]),
    .led3(A_REGISTER_data_stored[4]), .led4(A_REGISTER_data_stored[3]), .led5(A_REGISTER_data_stored[2]),
    .led6(A_REGISTER_data_stored[1]), .led7(A_REGISTER_data_stored[0]));
  LedBar ledbar_5 (
    .led0(B_REGISTER_data_stored[7]), .led1(B_REGISTER_data_stored[6]), .led2(B_REGISTER_data_stored[5]),
    .led3(B_REGISTER_data_stored[4]), .led4(B_REGISTER_data_stored[3]), .led5(B_REGISTER_data_stored[2]),
    .led6(B_REGISTER_data_stored[1]), .led7(B_REGISTER_data_stored[0]));
  ROM #(.dataWidth(12)) PC_DECODER (.addr(PROGRAM_COUNTER_REGISTER_p6), .data(PC_DECODER_data));
  ROM #(.dataWidth(12)) OUTPUT_REGISTER_DECODER (
    .addr(OUTPUT_REGISTER_data_stored), .data(OUTPUT_REGISTER_DECODER_data));
  LedBar ledbar_6 (
    .led0(ALU_alu_stored_output[7]), .led1(ALU_alu_stored_output[6]), .led2(ALU_alu_stored_output[5]),
    .led3(ALU_alu_stored_output[4]), .led4(ALU_alu_stored_output[3]), .led5(ALU_alu_stored_output[2]),
    .led6(ALU_alu_stored_output[1]), .led7(ALU_alu_stored_output[0]));
  LedBar ledbar_7 (
    .led0(MEMORY_ADRESS_REGISTER_data_stored[7]), .led1(MEMORY_ADRESS_REGISTER_data_stored[6]),
    .led2(MEMORY_ADRESS_REGISTER_data_stored[5]), .led3(MEMORY_ADRESS_REGISTER_data_stored[4]),
    .led4(MEMORY_ADRESS_REGISTER_data_stored[3]), .led5(MEMORY_ADRESS_REGISTER_data_stored[2]),
    .led6(MEMORY_ADRESS_REGISTER_data_stored[1]), .led7(MEMORY_ADRESS_REGISTER_data_stored[0]));
  LedBar ledbar_8 (
    .led0(controlled_buffer_3_out[7]), .led1(controlled_buffer_3_out[6]), .led2(controlled_buffer_3_out[5]),
    .led3(controlled_buffer_3_out[4]), .led4(controlled_buffer_3_out[3]), .led5(controlled_buffer_3_out[2]),
    .led6(controlled_buffer_3_out[1]), .led7(controlled_buffer_3_out[0]));
  LedBar ledbar_9 (
    .led0(OPERAND_REGISTER_data_stored[7]), .led1(OPERAND_REGISTER_data_stored[6]),
    .led2(OPERAND_REGISTER_data_stored[5]), .led3(OPERAND_REGISTER_data_stored[4]),
    .led4(OPERAND_REGISTER_data_stored[3]), .led5(OPERAND_REGISTER_data_stored[2]),
    .led6(OPERAND_REGISTER_data_stored[1]), .led7(OPERAND_REGISTER_data_stored[0]));
  Hex_Digit_Display #(.decimalPoint("false")) hex_digit_display_7 (.value(PC_DECODER_data[11:8]));
  Hex_Digit_Display #(.decimalPoint("false")) hex_digit_display_8 (.value(OUTPUT_REGISTER_DECODER_data[11:8]));
  Hex_Digit_Display #(.decimalPoint("false")) hex_digit_display_9 (.value(PC_DECODER_data[7:4]));
  Hex_Digit_Display #(.decimalPoint("false")) hex_digit_display_10 (.value(PC_DECODER_data[3:0]));
  Hex_Digit_Display #(.decimalPoint("false")) hex_digit_display_11 (.value(OUTPUT_REGISTER_DECODER_data[7:4]));
  Hex_Digit_Display #(.decimalPoint("false")) hex_digit_display_12 (.value(OUTPUT_REGISTER_DECODER_data[3:0]));
  Hex_Digit_Display hex_digit_display_13 (.value(PROGRAM_COUNTER_REGISTER_p6[7:4]));  // open: dp
  Hex_Digit_Display hex_digit_display_14 (.value(PROGRAM_COUNTER_REGISTER_p6[3:0]));  // open: dp
  Hex_Digit_Display hex_digit_display_15 (.value(OUTPUT_REGISTER_data_stored[7:4]));  // open: dp
  Hex_Digit_Display hex_digit_display_16 (.value(OUTPUT_REGISTER_data_stored[3:0]));  // open: dp

  // Notes on the sheet:
  //   Inverted Clock
  //   contents of CONTROL_LOGIC_ROM4 (hex, n*v repeats v):
  //   4f f5 14*df 4f f5 4f f6 cf d7 10*df 4f f5 4f f6 cf d7 10*df 4f f5 14*df 4f f5 14*df 4f f5 4f f6
  //   12*df 4f f5 4f f6 12*df 4f f5 14*df 4f f5 4f f6 9f 11*df 4f f5 14*df 4f f5 14*df 4f f5 14*df 4f f5
  //   4f f6 cf db 10*df 4f f5 4f f6 cf db 10*df 4f f5 14*df 4f f5 4f f6 12*df 4f f5 4f f6 12*df 4f f5 4f
  //   f6 12*df 4f f5 4f f6 12*df 4f f5 4f f6 12*df 4f f5 4f f6 9f 11*df 4f f5 4f f6 9f 11*df 4f f5 4f f6
  //   9f 11*df 4f f5 4f f6 9f 11*df 4f f5 4f f6 cf d7 10*df 4f f5 4f f6 12*df 4f f5 4f f6 cf db 10*df 4f
  //   f5 14*df 4f f5 14*df 4f f5 14*df 4f f5 14*df 4f f5 14*df 4f f5 14*df 4f f5 14*df 4f f5 4f f6 12*df
  //   4f f5 4f f6 12*df 4f f5 14*df 4f f5 4f f7 4f f7 4f f7 8*df 3488*0 4f f5 14*df 4f f5 4f f6 cf d7
  //   10*df 4f f5 4f f6 cf d7 10*df 4f f5 14*df 4f f5 14*df 4f f5 4f f6 12*df 4f f5 4f f6 12*df 4f f5
  //   14*df 4f f5 4f f6 9f 11*df 4f f5 14*df 4f f5 14*df 4f f5 14*df 4f f5 4f f6 cf db 10*df 4f f5 4f f6
  //   cf db 10*df 4f f5 14*df 4f f5 4f f6 12*df 4f f5 4f f6 9f 11*df 4f f5 4f f6 9f 11*df 4f f5 4f f6 9f
  //   11*df 4f f5 4f f6 9f 11*df 4f f5 4f f6 12*df 4f f5 4f f6 12*df 4f f5 4f f6 12*df 4f f5 4f f6 12*df
  //   4f f5 4f f6 cf d7 10*df 4f f5 4f f6 12*df 4f f5 4f f6 cf db 10*df 4f f5 14*df 4f f5 14*df 4f f5
  //   14*df 4f f5 14*df 4f f5 14*df 4f f5 14*df 4f f5 14*df 4f f5 4f f6 12*df 4f f5 4f f6 12*df 4f f5
  //   14*df 4f f5 4f f7 4f f7 4f f7 8*df
  //   contents of CONTROL_LOGIC_ROM3 (hex, n*v repeats v):
  //   20*f8 78 b8 14*f8 78 e8 12*f8 b8 15*f8 b9 17*f8 38 15*f8 68 13*f8 d8 17*f8 78 13*f8 ba 15*f8 be
  //   15*f8 bc 17*f8 78 d8 14*f8 78 f0 30*f8 68 b8 14*f8 b8 68 f9 13*f8 b8 68 f9 13*f8 b8 68 f9 13*f8 b8
  //   68 f9 13*f8 78 15*f8 78 15*f8 78 15*f8 78 15*f8 78 15*f8 78 15*f8 78 29*f8 c8 15*f8 d8 15*f8 b0
  //   15*f8 f0 15*f8 b8 15*f8 e8 17*f8 b8 68 f9 13*f8 b8 68 f9 11*f8 b8 29*f8 3488*0 20*f8 78 b8 14*f8 78
  //   e8 12*f8 b8 15*f8 b9 17*f8 38 15*f8 68 13*f8 d8 17*f8 78 13*f8 ba 15*f8 be 15*f8 bc 17*f8 78 d8
  //   14*f8 78 f0 30*f8 68 b8 14*f8 78 15*f8 78 15*f8 78 15*f8 78 15*f8 b8 68 f9 13*f8 b8 68 f9 13*f8 b8
  //   68 f9 13*f8 b8 68 f9 13*f8 78 15*f8 78 15*f8 78 29*f8 c8 15*f8 d8 15*f8 b0 15*f8 f0 15*f8 b8 15*f8
  //   e8 17*f8 b8 68 f9 13*f8 b8 68 f9 11*f8 b8 29*f8
  //   contents of CONTROL_LOGIC_ROM2 (hex, n*v repeats v):
  //   8e 8e ae 13*9e 5*8e ae 10*9e 5*8e ae 10*9e 8e 8e 26 13*9e 8e 8e 26 13*9e 4*8e ae 11*9e 4*8e ae 11*9e
  //   8e 8e ee 13*9e 4*8e ae 11*9e 8e 8e 26 13*9e 8e 8e 26 13*9e 8e 8e 26 13*9e 5*8e ae 10*9e 5*8e ae
  //   10*9e 8e 8e 14*9e 5*8e 26 10*9e 4*8e 8c 8e 2a 9*9e 4*8e 8c 8e 2a 9*9e 4*8e 8c 8e 2a 9*9e 4*8e 8c 8e
  //   2a 9*9e 4*8e ae 11*9e 4*8e ae 11*9e 4*8e ae 11*9e 4*8e ae 11*9e 5*8e aa 10*9e 4*8e aa 11*9e 5*8e ac
  //   10*9e 8e 8e ae 13*9e 8e 8e ae 13*9e 8e 8e aa 13*9e 8e 8e ae 13*9e 8e 8e aa 13*9e 8e 8e ac 13*9e 8e
  //   8e ac 13*9e 4*8e 8c 8e 2a 9*9e 4*8e 8c 8e 2a 9*9e 8e 8e 8e ae 12*9e 7*8e ae 8*9e 3488*0 8e 8e ae
  //   13*9e 5*8e ae 10*9e 5*8e ae 10*9e 8e 8e 26 13*9e 8e 8e 26 13*9e 4*8e ae 11*9e 4*8e ae 11*9e 8e 8e ee
  //   13*9e 4*8e ae 11*9e 8e 8e 26 13*9e 8e 8e 26 13*9e 8e 8e 26 13*9e 5*8e ae 10*9e 5*8e ae 10*9e 8e 8e
  //   14*9e 5*8e 26 10*9e 4*8e ae 11*9e 4*8e ae 11*9e 4*8e ae 11*9e 4*8e ae 11*9e 4*8e 8c 8e 2a 9*9e 4*8e
  //   8c 8e 2a 9*9e 4*8e 8c 8e 2a 9*9e 4*8e 8c 8e 2a 9*9e 5*8e aa 10*9e 4*8e aa 11*9e 5*8e ac 10*9e 8e 8e
  //   ae 13*9e 8e 8e ae 13*9e 8e 8e aa 13*9e 8e 8e ae 13*9e 8e 8e aa 13*9e 8e 8e ac 13*9e 8e 8e ac 13*9e
  //   4*8e 8c 8e 2a 9*9e 4*8e 8c 8e 2a 9*9e 8e 8e 8e ae 12*9e 7*8e ae 8*9e
  //   contents of CONTROL_LOGIC_ROM1 (hex, n*v repeats v):
  //   578*10 0 30 15*10 d0 10 90 10 50 8*10 3488*0 578*10 0 30 15*10 d0 10 90 10 50 8*10
  //   IDLE
  //   00 - ADD/SUB
  //   01 - AND
  //   10 - XOR
  //   11 - OR
  //   ALU_CARRY
  //   ALU_NEGATIVE
  //   ALU_ZERO
  //   ALU_OVERFLOW
  //   HALT SIGNAL
  //   contents of PC_DECODER (hex, n*v repeats v):
  //   0 1 2 3 4 5 6 7 8 9 10 11 12 13 14 15 16 17 18 19 20 21 22 23 24 25 26 27 28 29 30 31 32 33 34 35 36
  //   37 38 39 40 41 42 43 44 45 46 47 48 49 50 51 52 53 54 55 56 57 58 59 60 61 62 63 64 65 66 67 68 69
  //   70 71 72 73 74 75 76 77 78 79 80 81 82 83 84 85 86 87 88 89 90 91 92 93 94 95 96 97 98 99 100 101
  //   102 103 104 105 106 107 108 109 110 111 112 113 114 115 116 117 118 119 120 121 122 123 124 125 126
  //   127 128 129 130 131 132 133 134 135 136 137 138 139 140 141 142 143 144 145 146 147 148 149 150 151
  //   152 153 154 155 156 157 158 159 160 161 162 163 164 165 166 167 168 169 170 171 172 173 174 175 176
  //   177 178 179 180 181 182 183 184 185 186 187 188 189 190 191 192 193 194 195 196 197 198 199 200 201
  //   202 203 204 205 206 207 208 209 210 211 212 213 214 215 216 217 218 219 220 221 222 223 224 225 226
  //   227 228 229 230 231 232 233 234 235 236 237 238 239 240 241 242 243 244 245 246 247 248 249 250 251
  //   252 253 254 255
  //   contents of OUTPUT_REGISTER_DECODER (hex, n*v repeats v):
  //   0 1 2 3 4 5 6 7 8 9 10 11 12 13 14 15 16 17 18 19 20 21 22 23 24 25 26 27 28 29 30 31 32 33 34 35 36
  //   37 38 39 40 41 42 43 44 45 46 47 48 49 50 51 52 53 54 55 56 57 58 59 60 61 62 63 64 65 66 67 68 69
  //   70 71 72 73 74 75 76 77 78 79 80 81 82 83 84 85 86 87 88 89 90 91 92 93 94 95 96 97 98 99 100 101
  //   102 103 104 105 106 107 108 109 110 111 112 113 114 115 116 117 118 119 120 121 122 123 124 125 126
  //   127 128 129 130 131 132 133 134 135 136 137 138 139 140 141 142 143 144 145 146 147 148 149 150 151
  //   152 153 154 155 156 157 158 159 160 161 162 163 164 165 166 167 168 169 170 171 172 173 174 175 176
  //   177 178 179 180 181 182 183 184 185 186 187 188 189 190 191 192 193 194 195 196 197 198 199 200 201
  //   202 203 204 205 206 207 208 209 210 211 212 213 214 215 216 217 218 219 220 221 222 223 224 225 226
  //   227 228 229 230 231 232 233 234 235 236 237 238 239 240 241 242 243 244 245 246 247 248 249 250 251
  //   252 253 254 255
endmodule

module register_module (
  input  CLEAR,
  input  INPUT_ENABLE,
  input  [7:0] DATA_IN,
  input  OUTPUT_ENABLE,
  input  CLOCK,
  output [7:0] DATA_STORED,
  output [7:0] DATA_OUT
);

  wire n74245_1_pin1;

  _74245 u_74245_1 (
    .pin1(n74245_1_pin1), .pin2(DATA_STORED[7]), .pin3(DATA_STORED[6]), .pin4(DATA_STORED[5]),
    .pin5(DATA_STORED[4]), .pin6(DATA_STORED[3]), .pin7(DATA_STORED[2]), .pin8(DATA_STORED[1]),
    .pin9(DATA_STORED[0]), .pin19(OUTPUT_ENABLE), .pin18(DATA_OUT[7]), .pin17(DATA_OUT[6]),
    .pin16(DATA_OUT[5]), .pin15(DATA_OUT[4]), .pin14(DATA_OUT[3]), .pin13(DATA_OUT[2]), .pin12(DATA_OUT[1]),
    .pin11(DATA_OUT[0]));
  IC74LS173 ic74ls173_1 (
    .OE1(1'b0), .OE2(1'b0), .D1(DATA_IN[0]), .IE1(INPUT_ENABLE), .IE2(INPUT_ENABLE), .D2(DATA_IN[1]),
    .CLK(CLOCK), .D3(DATA_IN[2]), .D4(DATA_IN[3]), .CLR(CLEAR), .Q1(DATA_STORED[0]), .Q2(DATA_STORED[1]),
    .Q3(DATA_STORED[2]), .Q4(DATA_STORED[3]));  // open: GND, VCC
  IC74LS173 ic74ls173_2 (
    .OE1(1'b0), .OE2(1'b0), .D1(DATA_IN[4]), .IE1(INPUT_ENABLE), .IE2(INPUT_ENABLE), .D2(DATA_IN[5]),
    .CLK(CLOCK), .D3(DATA_IN[6]), .D4(DATA_IN[7]), .CLR(CLEAR), .Q1(DATA_STORED[4]), .Q2(DATA_STORED[5]),
    .Q3(DATA_STORED[6]), .Q4(DATA_STORED[7]));  // open: GND, VCC
  // also tied to VCC on the sheet: n74245_1_pin1
endmodule

module alu_module (
  input  ALU_OP0,
  input  ALU_OP1,
  input  ALU_OE_N,
  input  [7:0] B_INPUT,
  input  SUB_SIGNAL,
  input  [7:0] A_INPUT,
  output OVERFLOW_FLAG,
  output ZERO_FLAG,
  output NEGATIVE_FLAG,
  output [7:0] ALU_OUTPUT,
  output CARRY_OUT,
  output [7:0] ALU_STORED_OUTPUT
);

  wire not_1_out, not_2_out, xor_17_out, xor_18_out;
  wire [7:0] adder_1_out, and_1_out, multiplexer_1_out, multiplexer_2_out, or_1_out, xor_1_out, xor_9_out;

  LedBar A_INPUT_BAR (
    .led0(A_INPUT[7]), .led1(A_INPUT[6]), .led2(A_INPUT[5]), .led3(A_INPUT[4]), .led4(A_INPUT[3]),
    .led5(A_INPUT[2]), .led6(A_INPUT[1]), .led7(A_INPUT[0]));
  LedBar B_INPUT_BAR (
    .led0(B_INPUT[7]), .led1(B_INPUT[6]), .led2(B_INPUT[5]), .led3(B_INPUT[4]), .led4(B_INPUT[3]),
    .led5(B_INPUT[2]), .led6(B_INPUT[1]), .led7(B_INPUT[0]));
  xor xor_1 (xor_1_out[0], B_INPUT[0], SUB_SIGNAL);
  xor xor_2 (xor_1_out[1], B_INPUT[1], SUB_SIGNAL);
  xor xor_3 (xor_1_out[2], B_INPUT[2], SUB_SIGNAL);
  xor xor_4 (xor_1_out[3], B_INPUT[3], SUB_SIGNAL);
  xor xor_5 (xor_1_out[4], B_INPUT[4], SUB_SIGNAL);
  xor xor_6 (xor_1_out[5], B_INPUT[5], SUB_SIGNAL);
  xor xor_7 (xor_1_out[6], B_INPUT[6], SUB_SIGNAL);
  xor xor_8 (xor_1_out[7], B_INPUT[7], SUB_SIGNAL);
  xor xor_9 (xor_9_out[0], B_INPUT[0], A_INPUT[0]);
  xor xor_10 (xor_9_out[1], B_INPUT[1], A_INPUT[1]);
  xor xor_11 (xor_9_out[2], B_INPUT[2], A_INPUT[2]);
  xor xor_12 (xor_9_out[3], B_INPUT[3], A_INPUT[3]);
  xor xor_13 (xor_9_out[4], B_INPUT[4], A_INPUT[4]);
  xor xor_14 (xor_9_out[5], B_INPUT[5], A_INPUT[5]);
  xor xor_15 (xor_9_out[6], B_INPUT[6], A_INPUT[6]);
  xor xor_16 (xor_9_out[7], B_INPUT[7], A_INPUT[7]);
  and and_1 (and_1_out[0], B_INPUT[0], A_INPUT[0]);
  and and_2 (and_1_out[1], B_INPUT[1], A_INPUT[1]);
  and and_3 (and_1_out[2], B_INPUT[2], A_INPUT[2]);
  and and_4 (and_1_out[3], B_INPUT[3], A_INPUT[3]);
  and and_5 (and_1_out[4], B_INPUT[4], A_INPUT[4]);
  and and_6 (and_1_out[5], B_INPUT[5], A_INPUT[5]);
  and and_7 (and_1_out[6], B_INPUT[6], A_INPUT[6]);
  and and_8 (and_1_out[7], B_INPUT[7], A_INPUT[7]);
  or or_1 (or_1_out[0], B_INPUT[0], A_INPUT[0]);
  or or_2 (or_1_out[1], B_INPUT[1], A_INPUT[1]);
  or or_3 (or_1_out[2], B_INPUT[2], A_INPUT[2]);
  or or_4 (or_1_out[3], B_INPUT[3], A_INPUT[3]);
  or or_5 (or_1_out[4], B_INPUT[4], A_INPUT[4]);
  or or_6 (or_1_out[5], B_INPUT[5], A_INPUT[5]);
  or or_7 (or_1_out[6], B_INPUT[6], A_INPUT[6]);
  or or_8 (or_1_out[7], B_INPUT[7], A_INPUT[7]);
  LedBar ADDER_WORD_BAR (
    .led0(adder_1_out[7]), .led1(adder_1_out[6]), .led2(adder_1_out[5]), .led3(adder_1_out[4]),
    .led4(adder_1_out[3]), .led5(adder_1_out[2]), .led6(adder_1_out[1]), .led7(adder_1_out[0]));
  Adder adder_1 (.a(xor_1_out), .b(A_INPUT), .out(adder_1_out), .cin(SUB_SIGNAL), .cout(CARRY_OUT));
  LedBar XOR_WORD_BAR (
    .led0(xor_9_out[7]), .led1(xor_9_out[6]), .led2(xor_9_out[5]), .led3(xor_9_out[4]), .led4(xor_9_out[3]),
    .led5(xor_9_out[2]), .led6(xor_9_out[1]), .led7(xor_9_out[0]));
  LedBar AND_WORD_BAR (
    .led0(and_1_out[7]), .led1(and_1_out[6]), .led2(and_1_out[5]), .led3(and_1_out[4]), .led4(and_1_out[3]),
    .led5(and_1_out[2]), .led6(and_1_out[1]), .led7(and_1_out[0]));
  LedBar OR_WORD_BAR (
    .led0(or_1_out[7]), .led1(or_1_out[6]), .led2(or_1_out[5]), .led3(or_1_out[4]), .led4(or_1_out[3]),
    .led5(or_1_out[2]), .led6(or_1_out[1]), .led7(or_1_out[0]));
  xor xor_17 (xor_17_out, A_INPUT[7], xor_1_out[7]);
  xor xor_18 (xor_18_out, A_INPUT[7], ALU_STORED_OUTPUT[7]);
  not not_1 (not_1_out, xor_17_out);
  and and_9 (OVERFLOW_FLAG, not_1_out, xor_18_out);
  Multiplexer #(.width(8)) multiplexer_1 (.in0(adder_1_out), .in1(xor_9_out), .out(multiplexer_1_out), .sel(ALU_OP0));
  Multiplexer #(.width(8)) multiplexer_2 (.in0(and_1_out), .in1(or_1_out), .out(multiplexer_2_out), .sel(ALU_OP0));
  nor nor_1 (ZERO_FLAG, ALU_STORED_OUTPUT[0], ALU_STORED_OUTPUT[1], ALU_STORED_OUTPUT[2], ALU_STORED_OUTPUT[3], ALU_STORED_OUTPUT[4], ALU_STORED_OUTPUT[5], ALU_STORED_OUTPUT[6], ALU_STORED_OUTPUT[7]);
  Multiplexer #(.width(8)) multiplexer_3 (
    .in0(multiplexer_1_out), .in1(multiplexer_2_out), .out(ALU_STORED_OUTPUT), .sel(ALU_OP1));
  not not_2 (not_2_out, ALU_OE_N);
  assign ALU_OUTPUT = not_2_out ? ALU_STORED_OUTPUT : 8'bz;  // Controlled_Buffer controlled_buffer_1

  assign NEGATIVE_FLAG = ALU_STORED_OUTPUT[7];

  // Notes on the sheet:
  //   A7
  //   B7 xor SUB
  //   ADDER WORD
  //   XOR WORD
  //   AND WORD
  //   OR WORD
  //   Result7
  //   ADDER / XOR MUXED
  //   AND / OR MUXED
  //   00 - ADD/SUB
  //   01 - AND
  //   10 - XOR
  //   11 - OR
  //   FINAL MUXED OUTPUT
endmodule

module counting_register_module (
  input  [7:0] PC_BUS_DATA_IN,
  input  CLEAR,
  input  CLOCK,
  input  OUTPUT_ENABLE_N,
  input  COUNT_ENABLE,
  input  PC_IE_LOW_N,
  input  PC_IE_HIGH_N,
  input  PC_ADDRESS_OE_N,
  input  MAR_ADDRESS_OE_N,
  input  MAR_IE_LOW_N,
  input  MAR_IE_HIGH_N,
  input  [7:0] MAR_BUS_DATA_IN
);

  wire ic74ls173_1_q1, ic74ls173_1_q2, ic74ls173_1_q3, ic74ls173_1_q4, ic74ls173_2_q1, ic74ls173_2_q2,
       ic74ls173_2_q3, ic74ls173_2_q4, ic74ls173_3_q1, ic74ls173_3_q2, ic74ls173_3_q3, ic74ls173_3_q4,
       ic74ls173_4_q1, ic74ls173_4_q2, ic74ls173_4_q3, ic74ls173_4_q4, n74161_1_pin1, n74161_1_pin7,
       n74161_1_pin10, n74161_2_pin10, n74161_3_pin10, n74245_1_pin1, n74245_1_pin2, n74245_1_pin3,
       n74245_1_pin4, n74245_1_pin5, n74245_1_pin6, n74245_1_pin7, n74245_1_pin8, n74245_1_pin9,
       n74245_1_pin11, n74245_1_pin12, n74245_1_pin13, n74245_1_pin14, n74245_1_pin15, n74245_1_pin16,
       n74245_1_pin17, n74245_1_pin18, n74245_2_pin1, n74245_2_pin2, n74245_2_pin3, n74245_2_pin4,
       n74245_2_pin5, n74245_2_pin6, n74245_2_pin7, n74245_2_pin8, n74245_2_pin9, n74245_2_pin11,
       n74245_2_pin12, n74245_2_pin13, n74245_2_pin14, n74245_2_pin15, n74245_2_pin16, n74245_2_pin17,
       n74245_2_pin18;

  _74245 u_74245_1 (
    .pin1(n74245_1_pin1), .pin2(n74245_1_pin2), .pin3(n74245_1_pin3), .pin4(n74245_1_pin4),
    .pin5(n74245_1_pin5), .pin6(n74245_1_pin6), .pin7(n74245_1_pin7), .pin8(n74245_1_pin8),
    .pin9(n74245_1_pin9), .pin19(PC_ADDRESS_OE_N), .pin18(n74245_1_pin18), .pin17(n74245_1_pin17),
    .pin16(n74245_1_pin16), .pin15(n74245_1_pin15), .pin14(n74245_1_pin14), .pin13(n74245_1_pin13),
    .pin12(n74245_1_pin12), .pin11(n74245_1_pin11));
  // AS6C62256 as6c62256_1: pin names not known
  IC74LS173 ic74ls173_1 (
    .OE1(MAR_ADDRESS_OE_N), .OE2(MAR_ADDRESS_OE_N), .D1(MAR_BUS_DATA_IN[4]), .IE1(MAR_IE_HIGH_N),
    .IE2(MAR_IE_HIGH_N), .D2(MAR_BUS_DATA_IN[5]), .CLK(CLOCK), .D3(MAR_BUS_DATA_IN[6]),
    .D4(MAR_BUS_DATA_IN[7]), .CLR(CLEAR), .Q1(ic74ls173_1_q1), .Q2(ic74ls173_1_q2), .Q3(ic74ls173_1_q3),
    .Q4(ic74ls173_1_q4));  // open: GND, VCC
  _74161 u_74161_1 (
    .pin1(n74161_1_pin1), .pin2(CLOCK), .pin3(PC_BUS_DATA_IN[4]), .pin4(PC_BUS_DATA_IN[5]),
    .pin5(PC_BUS_DATA_IN[6]), .pin6(PC_BUS_DATA_IN[7]), .pin7(n74161_1_pin7), .pin14(n74245_1_pin15),
    .pin13(n74245_1_pin16), .pin12(n74245_1_pin17), .pin11(n74245_1_pin18), .pin10(n74161_1_pin10),
    .pin9(PC_IE_HIGH_N));  // open: pin15
  IC74LS173 ic74ls173_2 (
    .OE1(MAR_ADDRESS_OE_N), .OE2(MAR_ADDRESS_OE_N), .D1(MAR_BUS_DATA_IN[0]), .IE1(MAR_IE_HIGH_N),
    .IE2(MAR_IE_HIGH_N), .D2(MAR_BUS_DATA_IN[1]), .CLK(CLOCK), .D3(MAR_BUS_DATA_IN[2]),
    .D4(MAR_BUS_DATA_IN[3]), .CLR(CLEAR), .Q1(ic74ls173_2_q1), .Q2(ic74ls173_2_q2), .Q3(ic74ls173_2_q3),
    .Q4(ic74ls173_2_q4));  // open: GND, VCC
  _74161 u_74161_2 (
    .pin1(n74161_1_pin1), .pin2(CLOCK), .pin3(PC_BUS_DATA_IN[0]), .pin4(PC_BUS_DATA_IN[1]),
    .pin5(PC_BUS_DATA_IN[2]), .pin6(PC_BUS_DATA_IN[3]), .pin7(n74161_1_pin7), .pin15(n74161_1_pin10),
    .pin14(n74245_1_pin11), .pin13(n74245_1_pin12), .pin12(n74245_1_pin13), .pin11(n74245_1_pin14),
    .pin10(n74161_2_pin10), .pin9(PC_IE_HIGH_N));
  _74245 u_74245_2 (
    .pin1(n74245_2_pin1), .pin2(n74245_2_pin2), .pin3(n74245_2_pin3), .pin4(n74245_2_pin4),
    .pin5(n74245_2_pin5), .pin6(n74245_2_pin6), .pin7(n74245_2_pin7), .pin8(n74245_2_pin8),
    .pin9(n74245_2_pin9), .pin19(PC_ADDRESS_OE_N), .pin18(n74245_2_pin18), .pin17(n74245_2_pin17),
    .pin16(n74245_2_pin16), .pin15(n74245_2_pin15), .pin14(n74245_2_pin14), .pin13(n74245_2_pin13),
    .pin12(n74245_2_pin12), .pin11(n74245_2_pin11));
  IC74LS173 ic74ls173_3 (
    .OE1(MAR_ADDRESS_OE_N), .OE2(MAR_ADDRESS_OE_N), .D1(MAR_BUS_DATA_IN[4]), .IE1(MAR_IE_LOW_N),
    .IE2(MAR_IE_LOW_N), .D2(MAR_BUS_DATA_IN[5]), .CLK(CLOCK), .D3(MAR_BUS_DATA_IN[6]),
    .D4(MAR_BUS_DATA_IN[7]), .CLR(CLEAR), .Q1(ic74ls173_3_q1), .Q2(ic74ls173_3_q2), .Q3(ic74ls173_3_q3),
    .Q4(ic74ls173_3_q4));  // open: GND, VCC
  _74161 u_74161_3 (
    .pin1(n74161_1_pin1), .pin2(CLOCK), .pin3(PC_BUS_DATA_IN[4]), .pin4(PC_BUS_DATA_IN[5]),
    .pin5(PC_BUS_DATA_IN[6]), .pin6(PC_BUS_DATA_IN[7]), .pin7(n74161_1_pin7), .pin15(n74161_2_pin10),
    .pin14(n74245_2_pin15), .pin13(n74245_2_pin16), .pin12(n74245_2_pin17), .pin11(n74245_2_pin18),
    .pin10(n74161_3_pin10), .pin9(PC_IE_LOW_N));
  IC74LS173 ic74ls173_4 (
    .OE1(MAR_ADDRESS_OE_N), .OE2(MAR_ADDRESS_OE_N), .D1(MAR_BUS_DATA_IN[0]), .IE1(MAR_IE_LOW_N),
    .IE2(MAR_IE_LOW_N), .D2(MAR_BUS_DATA_IN[1]), .CLK(CLOCK), .D3(MAR_BUS_DATA_IN[2]),
    .D4(MAR_BUS_DATA_IN[3]), .CLR(CLEAR), .Q1(ic74ls173_4_q1), .Q2(ic74ls173_4_q2), .Q3(ic74ls173_4_q3),
    .Q4(ic74ls173_4_q4));  // open: GND, VCC
  _74161 u_74161_4 (
    .pin1(n74161_1_pin1), .pin2(CLOCK), .pin3(PC_BUS_DATA_IN[0]), .pin4(PC_BUS_DATA_IN[1]),
    .pin5(PC_BUS_DATA_IN[2]), .pin6(PC_BUS_DATA_IN[3]), .pin7(n74161_1_pin7), .pin15(n74161_3_pin10),
    .pin14(n74245_2_pin11), .pin13(n74245_2_pin12), .pin12(n74245_2_pin13), .pin11(n74245_2_pin14),
    .pin10(COUNT_ENABLE), .pin9(PC_IE_LOW_N));
  not not_1 (n74161_1_pin1, CLEAR);
  // also tied to GND on the sheet: {n74245_1_pin1, n74245_2_pin1}
  // also tied to VCC on the sheet: n74161_1_pin7

  // Notes on the sheet:
  //   MAR_ADDRESS_OE_N: initial=0x1
  //   MAR_IE_LOW_N: initial=0x1
  //   MAR_IE_HIGH_N: initial=0x1
  //   PC_IE_LOW_N: initial=0x1
  //   PC_IE_HIGH_N: initial=0x1
endmodule

module ROM_16MB_x_8 (
  input  OE_N,
  input  RESET_N,
  input  [23:0] ADDRESS_IN,
  output [7:0] DATA_OUT
);

  wire not_1_out;
  wire [7:0] controlled_buffer_1_out, rom_1_data;

  not not_1 (not_1_out, OE_N);
  ROM #(.addrWidth(24)) rom_1 (.addr(ADDRESS_IN), .data(rom_1_data));
  assign controlled_buffer_1_out = RESET_N ? rom_1_data : 8'bz;  // Controlled_Buffer controlled_buffer_1
  assign DATA_OUT = not_1_out ? controlled_buffer_1_out : 8'bz;  // Controlled_Buffer controlled_buffer_2

  // Notes on the sheet:
  //   OE_N: initial=0x1
  //   RESET_N: initial=0x1
  //   contents of rom_1 (hex, n*v repeats v):
  //   12 34 1193044*0 a5
endmodule

module ROM_ADDRESS_REGISTER (
  input  INCREMENT,
  input  LOAD_S0,
  input  LOAD_S1,
  input  [7:0] ADDRESS_IN,
  input  CLK,
  input  CLEAR,
  output [23:0] ADDRESS_OUT
);

  wire n74139_1_pin1, n74139_1_pin5, n74139_1_pin6, n74139_1_pin7, n74161_1_pin7, n74161_1_pin15,
       n74161_2_pin15, n74161_3_pin15, n74161_4_pin15, n74161_5_pin15, not_1_out;

  _74139 u_74139_1 (
    .pin1(n74139_1_pin1), .pin2(LOAD_S0), .pin3(LOAD_S1), .pin5(n74139_1_pin5), .pin6(n74139_1_pin6),
    .pin7(n74139_1_pin7));  // open: pin4, pin15, pin14, pin13, pin12, pin11, pin10, pin9
  not not_1 (not_1_out, CLEAR);
  _74161 u_74161_1 (
    .pin1(not_1_out), .pin2(CLK), .pin3(ADDRESS_IN[0]), .pin4(ADDRESS_IN[1]), .pin5(ADDRESS_IN[2]),
    .pin6(ADDRESS_IN[3]), .pin7(n74161_1_pin7), .pin15(n74161_1_pin15), .pin14(ADDRESS_OUT[0]),
    .pin13(ADDRESS_OUT[1]), .pin12(ADDRESS_OUT[2]), .pin11(ADDRESS_OUT[3]), .pin10(INCREMENT),
    .pin9(n74139_1_pin5));
  _74161 u_74161_2 (
    .pin1(not_1_out), .pin2(CLK), .pin3(ADDRESS_IN[4]), .pin4(ADDRESS_IN[5]), .pin5(ADDRESS_IN[6]),
    .pin6(ADDRESS_IN[7]), .pin7(n74161_1_pin7), .pin15(n74161_2_pin15), .pin14(ADDRESS_OUT[4]),
    .pin13(ADDRESS_OUT[5]), .pin12(ADDRESS_OUT[6]), .pin11(ADDRESS_OUT[7]), .pin10(n74161_1_pin15),
    .pin9(n74139_1_pin5));
  _74161 u_74161_3 (
    .pin1(not_1_out), .pin2(CLK), .pin3(ADDRESS_IN[0]), .pin4(ADDRESS_IN[1]), .pin5(ADDRESS_IN[2]),
    .pin6(ADDRESS_IN[3]), .pin7(n74161_1_pin7), .pin15(n74161_3_pin15), .pin14(ADDRESS_OUT[8]),
    .pin13(ADDRESS_OUT[9]), .pin12(ADDRESS_OUT[10]), .pin11(ADDRESS_OUT[11]), .pin10(n74161_2_pin15),
    .pin9(n74139_1_pin6));
  _74161 u_74161_4 (
    .pin1(not_1_out), .pin2(CLK), .pin3(ADDRESS_IN[4]), .pin4(ADDRESS_IN[5]), .pin5(ADDRESS_IN[6]),
    .pin6(ADDRESS_IN[7]), .pin7(n74161_1_pin7), .pin15(n74161_4_pin15), .pin14(ADDRESS_OUT[12]),
    .pin13(ADDRESS_OUT[13]), .pin12(ADDRESS_OUT[14]), .pin11(ADDRESS_OUT[15]), .pin10(n74161_3_pin15),
    .pin9(n74139_1_pin6));
  _74161 u_74161_5 (
    .pin1(not_1_out), .pin2(CLK), .pin3(ADDRESS_IN[0]), .pin4(ADDRESS_IN[1]), .pin5(ADDRESS_IN[2]),
    .pin6(ADDRESS_IN[3]), .pin7(n74161_1_pin7), .pin15(n74161_5_pin15), .pin14(ADDRESS_OUT[16]),
    .pin13(ADDRESS_OUT[17]), .pin12(ADDRESS_OUT[18]), .pin11(ADDRESS_OUT[19]), .pin10(n74161_4_pin15),
    .pin9(n74139_1_pin7));
  _74161 u_74161_6 (
    .pin1(not_1_out), .pin2(CLK), .pin3(ADDRESS_IN[4]), .pin4(ADDRESS_IN[5]), .pin5(ADDRESS_IN[6]),
    .pin6(ADDRESS_IN[7]), .pin7(n74161_1_pin7), .pin14(ADDRESS_OUT[20]), .pin13(ADDRESS_OUT[21]),
    .pin12(ADDRESS_OUT[22]), .pin11(ADDRESS_OUT[23]), .pin10(n74161_5_pin15), .pin9(n74139_1_pin7));  // open: pin15
  // also tied to GND on the sheet: n74139_1_pin1
  // also tied to VCC on the sheet: n74161_1_pin7
endmodule

module VRAM_ADDRESS_REGISTER (
  input  INCREMENT,
  input  LOAD_S0,
  input  LOAD_S1,
  input  [7:0] ADDRESS_IN,
  input  CLK,
  input  CLEAR,
  output [11:0] ADDRESS_OUT
);

  wire n74161_1_pin7, n74161_1_pin15, n74161_2_pin15, n74161_3_pin15, not_1_out, not_2_out;

  not not_1 (not_1_out, INCREMENT);
  not not_2 (not_2_out, CLEAR);
  _74161 u_74161_1 (
    .pin1(not_2_out), .pin2(CLK), .pin3(ADDRESS_IN[0]), .pin4(ADDRESS_IN[1]), .pin5(ADDRESS_IN[2]),
    .pin6(ADDRESS_IN[3]), .pin7(n74161_1_pin7), .pin15(n74161_1_pin15), .pin14(ADDRESS_OUT[11]),
    .pin13(ADDRESS_OUT[10]), .pin12(ADDRESS_OUT[9]), .pin11(ADDRESS_OUT[8]), .pin10(not_1_out), .pin9(LOAD_S1));
  _74161 u_74161_2 (
    .pin1(not_2_out), .pin2(CLK), .pin3(ADDRESS_IN[4]), .pin4(ADDRESS_IN[5]), .pin5(ADDRESS_IN[6]),
    .pin6(ADDRESS_IN[7]), .pin7(n74161_1_pin7), .pin15(n74161_2_pin15), .pin14(ADDRESS_OUT[7]),
    .pin13(ADDRESS_OUT[6]), .pin12(ADDRESS_OUT[5]), .pin11(ADDRESS_OUT[4]), .pin10(n74161_1_pin15),
    .pin9(LOAD_S1));
  _74161 u_74161_3 (
    .pin1(not_2_out), .pin2(CLK), .pin3(ADDRESS_IN[0]), .pin4(ADDRESS_IN[1]), .pin5(ADDRESS_IN[2]),
    .pin6(ADDRESS_IN[3]), .pin7(n74161_1_pin7), .pin15(n74161_3_pin15), .pin14(ADDRESS_OUT[3]),
    .pin13(ADDRESS_OUT[2]), .pin12(ADDRESS_OUT[1]), .pin11(ADDRESS_OUT[0]), .pin10(n74161_2_pin15),
    .pin9(LOAD_S0));
  // also tied to VCC on the sheet: n74161_1_pin7

  // Notes on the sheet:
  //   INCREMENT: initial=0x1
  //   LOAD_S0: initial=0x1
  //   LOAD_S1: initial=0x1
endmodule
